// Logisim project cpu.circ as structural Verilog
module main (
  input  reset,
  input  [15:0] in_2
);

  wire alu_1_z, ALUinB, and_1_out, and_2_out, and_3_out, BLE, BNE, BR, clk, DMwe, input_kbd, JAL, JP, JR,
       kbdvalid, memory_latch_1_oe_latched, memory_latch_1_we_latched, not_1_out, not_2_out, not_3_out,
       not_4_out, op0, op1, op2, op3, op4, op5, op6, op7, op15, or_1_out, or_2_out, Rdst, Rwd, RWe, sftimm;
  wire [2:0] ALUop, multiplexer_6_out, multiplexer_7_out;
  wire [3:0] opCode;
  wire [5:0] immd, multiplexer_8_out;
  wire [6:0] keyboard_1_data;
  wire [11:6] immdj;
  wire [15:0] adder_pc_1_out_2, adder_pc_2_out_2, adder_sub_1_result, alu_1_result, kbdout,
       memory_latch_1_address_latched, memory_latch_1_data_in_latched, multiplexer_1_out, multiplexer_2_out,
       multiplexer_3_out, multiplexer_4_out, multiplexer_5_out, multiplexer_9_out, multiplexer_10_out,
       multiplexer_11_out, multiplexer_12_out, PCT, ram_1_dout, registerfile_1_dataout2,
       sign_extender_1_out_ext, ttydata, zero_extender_2_out_2, zero_extender_3_out_2;

  Clock clock_1 (.out(clk));
  not not_1 (not_1_out, clk);
  not not_2 (not_2_out, clk);
  Keyboard keyboard_1 (.clk(not_2_out), .clr(reset), .avail(kbdvalid), .data(keyboard_1_data));  // open: re
  adder_pc adder_pc_1 (.out_2(adder_pc_1_out_2), .pc_val(PCT));
  zero_extender zero_extender_1 (.out_2(kbdout), .in_1({{5{1'b0}}, keyboard_1_data}));
  // Probe on PCT
  singleRegister singleregister_1 (
    .clk(not_1_out), .reset(reset), .WrtEn(1'b1), .datain(multiplexer_1_out), .dataout(PCT));
  ROM #(.addrWidth(16), .dataWidth(16)) rom_1 (.addr(PCT), .data({opCode, immdj, immd}));
  TTY #(.rows(13), .cols(80)) tty_1 (.data(ttydata[6:0]), .clk(clk), .we(op15), .clr(reset));
  Multiplexer #(.width(16), .enable("false")) multiplexer_1 (
    .in0(multiplexer_5_out), .in1(zero_extender_2_out_2), .out(multiplexer_1_out), .sel(JAL));
  zero_extender zero_extender_2 (.out_2(zero_extender_2_out_2), .in_1({immdj, immd}));
  adder_pc adder_pc_2 (.out_2(adder_pc_2_out_2), .pc_val(PCT));
  Multiplexer #(.width(16), .enable("false")) multiplexer_2 (
    .in0(16'h80), .in1(kbdout), .out(multiplexer_2_out), .sel(kbdvalid));
  Multiplexer #(.width(16), .enable("false")) multiplexer_3 (
    .in0(multiplexer_12_out), .in1(adder_pc_2_out_2), .out(multiplexer_3_out), .sel(JAL));
  Multiplexer #(.width(16), .enable("false")) multiplexer_4 (
    .in0(multiplexer_3_out), .in1(multiplexer_2_out), .out(multiplexer_4_out), .sel(input_kbd));
  Decoder #(.select(4), .enable("false")) decoder_1 (
    .out0(op0), .out1(op1), .out2(op2), .out3(op3), .out4(op4), .out5(op5), .out6(op6), .out7(op7),
    .out8(DMwe), .out9(BNE), .out10(BLE), .out11(JP), .out12(JR), .out13(JAL), .out14(input_kbd),
    .out15(op15), .sel(opCode));
  Multiplexer #(.width(16), .enable("false")) multiplexer_5 (
    .in0(multiplexer_11_out), .in1(ttydata), .out(multiplexer_5_out), .sel(JR));
  Multiplexer #(.width(3), .enable("false")) multiplexer_6 (
    .in0(multiplexer_7_out), .in1(3'b111), .out(multiplexer_6_out), .sel(JAL));
  Multiplexer #(.width(3), .enable("false")) multiplexer_7 (
    .in0(immdj[8:6]), .in1(immd[5:3]), .out(multiplexer_7_out), .sel(Rdst));
  RegisterFile registerfile_1 (
    .read02(immdj[8:6]), .datain(multiplexer_4_out), .WriteEnable(RWe), .reset(reset),
    .writereg(multiplexer_6_out), .dataout2(registerfile_1_dataout2), .dataout1(ttydata), .clk(clk),
    .read01(immdj[11:9]));
  sign_extender sign_extender_1 (.out_ext(sign_extender_1_out_ext), .in_ext(multiplexer_8_out));
  Multiplexer #(.width(6), .enable("false")) multiplexer_8 (
    .in0(immd), .in1({3'b000, immd[2:0]}), .out(multiplexer_8_out), .sel(sftimm));
  Multiplexer #(.width(16), .enable("false")) multiplexer_9 (
    .in0(registerfile_1_dataout2), .in1(sign_extender_1_out_ext), .out(multiplexer_9_out), .sel(ALUinB));
  adder_sub adder_sub_1 (
    .A(adder_pc_1_out_2), .B(sign_extender_1_out_ext), .result(adder_sub_1_result));  // open: sub, unsigned_ovf, signed_ovf, z
  and and_1 (and_1_out, not_3_out, BNE);
  not not_3 (not_3_out, alu_1_z);
  and and_2 (and_2_out, or_1_out, BR);
  or or_1 (or_1_out, and_1_out, and_3_out);
  ALU alu_1 (.z(alu_1_z), .in1(ttydata), .ALUop(ALUop), .in2(multiplexer_9_out), .result(alu_1_result));
  Multiplexer #(.width(16), .enable("false")) multiplexer_10 (
    .in0(adder_pc_1_out_2), .in1(adder_sub_1_result), .out(multiplexer_10_out), .sel(and_2_out));
  and and_3 (and_3_out, or_2_out, BLE);
  or or_2 (or_2_out, alu_1_z, alu_1_result[15]);
  or or_3 (ALUop[0], op2, BNE, op4, BLE, op6);
  or or_4 (ALUop[1], op3, op4);
  zero_extender zero_extender_3 (.out_2(zero_extender_3_out_2), .in_1({immdj, immd}));
  or or_5 (ALUop[2], op5, op6);
  Multiplexer #(.width(16), .enable("false")) multiplexer_11 (
    .in0(multiplexer_10_out), .in1(zero_extender_3_out_2), .out(multiplexer_11_out), .sel(JP));
  Multiplexer #(.width(16), .enable("false")) multiplexer_12 (
    .in0(alu_1_result), .in1(ram_1_dout), .out(multiplexer_12_out), .sel(Rwd));
  not not_4 (not_4_out, clk);
  or or_6 (RWe, input_kbd, DMwe, op0, op1, op2, op6, op3, op4, op5, op7, JAL);
  or or_7 (Rdst, op0, op2, op3, op4, op5, op6, DMwe);
  or or_8 (ALUinB, op1, op3, op4, op7, DMwe);
  or or_9 (sftimm, op3, op4);
  buf or_10 (Rwd, op7);  // OR_Gate
  or or_11 (BR, BNE, BLE);
  memory_latch memory_latch_1 (
    .address(alu_1_result), .WE(DMwe), .clk(not_4_out), .data_in(registerfile_1_dataout2),
    .address_latched(memory_latch_1_address_latched), .WE_latched(memory_latch_1_we_latched),
    .OE_latched(memory_latch_1_oe_latched), .data_in_latched(memory_latch_1_data_in_latched));
  RAM #(.addrWidth(16), .dataWidth(16), .trigger("high"), .databus("bibus")) ram_1 (
    .addr(memory_latch_1_address_latched), .we(memory_latch_1_we_latched), .oe(memory_latch_1_oe_latched),
    .din(memory_latch_1_data_in_latched), .dout(ram_1_dout));

  // Other names for the same wires on the sheet: immdj[5:0] = immd; rd[2:0] = immd[5:3]; rt[2:0] = immdj[8:6];
  //   rs[2:0] = immdj[11:9]; op8 = DMwe; op9 = BNE; op10 = BLE; op11 = JP; op12 = JR; op13 = JAL; op14 = input_kbd;
  //   outtty = op15; sftmnt[2:0] = immd[2:0]

  // Notes on the sheet:
  //   PC
  //   contents of rom_1 (hex, n*v repeats v):
  //   1 10 100 1 0 10 1001 1000
  //   do I need a sll of 1 here?
  //   add
  //   sub
  //   addi
  //   sll
  //   and
  //   srl
  //   not
  //   lw
  //   bne
  //   sw
endmodule

module RegisterFile (
  input  reset,
  input  clk,
  input  WriteEnable,
  input  [2:0] read01,
  input  [15:0] datain,
  input  [2:0] writereg,
  input  [2:0] read02,
  output [15:0] dataout1,
  output [15:0] dataout2
);

  wire clk_t, decoder_1_out1, decoder_1_out2, decoder_1_out3, decoder_1_out4, decoder_1_out5, decoder_1_out6,
       decoder_1_out7, r10, r11, r12, r13, r14, r15, r16, r17, r20, r21, r22, r23, r24, r25, r26, r27;
  wire [15:0] reg0_dataout, reg1_dataout, reg2_dataout, reg3_dataout, reg4_dataout, reg5_dataout,
       reg6_dataout, reg7_dataout;

  and and_1 (clk_t, clk, WriteEnable);
  Decoder #(.select(3), .enable("false")) decoder_1 (
    .out1(decoder_1_out1), .out2(decoder_1_out2), .out3(decoder_1_out3), .out4(decoder_1_out4),
    .out5(decoder_1_out5), .out6(decoder_1_out6), .out7(decoder_1_out7), .sel(writereg));  // open: out0
  // Probe on reg7_dataout
  singleRegister reg7 (.clk(clk_t), .reset(reset), .WrtEn(decoder_1_out7), .datain(datain), .dataout(reg7_dataout));
  // Probe on reg6_dataout
  singleRegister reg6 (.clk(clk_t), .reset(reset), .WrtEn(decoder_1_out6), .datain(datain), .dataout(reg6_dataout));
  // Probe on reg5_dataout
  singleRegister reg5 (.clk(clk_t), .reset(reset), .WrtEn(decoder_1_out5), .datain(datain), .dataout(reg5_dataout));
  // Probe on reg4_dataout
  singleRegister reg4 (.clk(clk_t), .reset(reset), .WrtEn(decoder_1_out4), .datain(datain), .dataout(reg4_dataout));
  // Probe on reg3_dataout
  singleRegister reg3 (.clk(clk_t), .reset(reset), .WrtEn(decoder_1_out3), .datain(datain), .dataout(reg3_dataout));
  // Probe on reg2_dataout
  singleRegister reg2 (.clk(clk_t), .reset(reset), .WrtEn(decoder_1_out2), .datain(datain), .dataout(reg2_dataout));
  // Probe on reg1_dataout
  singleRegister reg1 (.clk(clk_t), .reset(reset), .WrtEn(decoder_1_out1), .datain(datain), .dataout(reg1_dataout));
  // Probe on reg0_dataout
  singleRegister reg0 (.clk(clk_t), .reset(reset), .WrtEn(1'b0), .datain({16{1'b0}}), .dataout(reg0_dataout));
  assign dataout1 = r17 ? reg7_dataout : 16'bz;  // Controlled_Buffer controlled_buffer_1
  assign dataout1 = r16 ? reg6_dataout : 16'bz;  // Controlled_Buffer controlled_buffer_2
  assign dataout1 = r15 ? reg5_dataout : 16'bz;  // Controlled_Buffer controlled_buffer_3
  assign dataout1 = r14 ? reg4_dataout : 16'bz;  // Controlled_Buffer controlled_buffer_4
  assign dataout1 = r13 ? reg3_dataout : 16'bz;  // Controlled_Buffer controlled_buffer_5
  assign dataout1 = r12 ? reg2_dataout : 16'bz;  // Controlled_Buffer controlled_buffer_6
  assign dataout1 = r11 ? reg1_dataout : 16'bz;  // Controlled_Buffer controlled_buffer_7
  assign dataout1 = r10 ? reg0_dataout : 16'bz;  // Controlled_Buffer controlled_buffer_8
  assign dataout2 = r27 ? reg7_dataout : 16'bz;  // Controlled_Buffer controlled_buffer_9
  assign dataout2 = r26 ? reg6_dataout : 16'bz;  // Controlled_Buffer controlled_buffer_10
  assign dataout2 = r25 ? reg5_dataout : 16'bz;  // Controlled_Buffer controlled_buffer_11
  assign dataout2 = r24 ? reg4_dataout : 16'bz;  // Controlled_Buffer controlled_buffer_12
  assign dataout2 = r23 ? reg3_dataout : 16'bz;  // Controlled_Buffer controlled_buffer_13
  assign dataout2 = r22 ? reg2_dataout : 16'bz;  // Controlled_Buffer controlled_buffer_14
  assign dataout2 = r21 ? reg1_dataout : 16'bz;  // Controlled_Buffer controlled_buffer_15
  assign dataout2 = r20 ? reg0_dataout : 16'bz;  // Controlled_Buffer controlled_buffer_16
  Decoder #(.select(3), .enable("false")) decoder_2 (
    .out0(r10), .out1(r11), .out2(r12), .out3(r13), .out4(r14), .out5(r15), .out6(r16), .out7(r17),
    .sel(read01));
  Decoder #(.select(3), .enable("false")) decoder_3 (
    .out0(r20), .out1(r21), .out2(r22), .out3(r23), .out4(r24), .out5(r25), .out6(r26), .out7(r27),
    .sel(read02));

  // Other names for the same wires on the sheet: R = reset
endmodule

module singleRegister (
  input  clk,
  input  reset,
  input  WrtEn,
  input  [15:0] datain,
  output [15:0] dataout
);

  wire clkin;

  and and_1 (clkin, clk, WrtEn);
  D_Flip_Flop d_ff_1 (.D(datain[15]), .clk(clkin), .Q(dataout[15]), .reset(reset));  // open: Qn, preset
  D_Flip_Flop d_ff_2 (.D(datain[13]), .clk(clkin), .Q(dataout[13]), .reset(reset));  // open: Qn, preset
  D_Flip_Flop d_ff_3 (.D(datain[11]), .clk(clkin), .Q(dataout[11]), .reset(reset));  // open: Qn, preset
  D_Flip_Flop d_ff_4 (.D(datain[9]), .clk(clkin), .Q(dataout[9]), .reset(reset));  // open: Qn, preset
  D_Flip_Flop d_ff_5 (.D(datain[7]), .clk(clkin), .Q(dataout[7]), .reset(reset));  // open: Qn, preset
  D_Flip_Flop d_ff_6 (.D(datain[5]), .clk(clkin), .Q(dataout[5]), .reset(reset));  // open: Qn, preset
  D_Flip_Flop d_ff_7 (.D(datain[3]), .clk(clkin), .Q(dataout[3]), .reset(reset));  // open: Qn, preset
  D_Flip_Flop d_ff_8 (.D(datain[1]), .clk(clkin), .Q(dataout[1]), .reset(reset));  // open: Qn, preset
  D_Flip_Flop d_ff_9 (.D(datain[14]), .clk(clkin), .Q(dataout[14]), .reset(reset));  // open: Qn, preset
  D_Flip_Flop d_ff_10 (.D(datain[12]), .clk(clkin), .Q(dataout[12]), .reset(reset));  // open: Qn, preset
  D_Flip_Flop d_ff_11 (.D(datain[10]), .clk(clkin), .Q(dataout[10]), .reset(reset));  // open: Qn, preset
  D_Flip_Flop d_ff_12 (.D(datain[8]), .clk(clkin), .Q(dataout[8]), .reset(reset));  // open: Qn, preset
  D_Flip_Flop d_ff_13 (.D(datain[6]), .clk(clkin), .Q(dataout[6]), .reset(reset));  // open: Qn, preset
  D_Flip_Flop d_ff_14 (.D(datain[4]), .clk(clkin), .Q(dataout[4]), .reset(reset));  // open: Qn, preset
  D_Flip_Flop d_ff_15 (.D(datain[2]), .clk(clkin), .Q(dataout[2]), .reset(reset));  // open: Qn, preset
  D_Flip_Flop d_ff_16 (.D(datain[0]), .clk(clkin), .Q(dataout[0]), .reset(reset));  // open: Qn, preset

  // Other names for the same wires on the sheet: b0 = datain[0]; b1 = datain[1]; b2 = datain[2]; b3 = datain[3];
  //   b4 = datain[4]; b5 = datain[5]; b6 = datain[6]; b7 = datain[7]; b8 = datain[8]; b9 = datain[9];
  //   b10 = datain[10]; b11 = datain[11]; b12 = datain[12]; b13 = datain[13]; b14 = datain[14]; b15 = datain[15];
  //   o0 = dataout[0]; o1 = dataout[1]; o2 = dataout[2]; o3 = dataout[3]; o4 = dataout[4]; o5 = dataout[5];
  //   o6 = dataout[6]; o7 = dataout[7]; o8 = dataout[8]; o9 = dataout[9]; o10 = dataout[10]; o11 = dataout[11];
  //   o12 = dataout[12]; o13 = dataout[13]; o14 = dataout[14]; o15 = dataout[15]
endmodule

module ALU (
  input  [2:0] ALUop,
  input  [15:0] in1,
  input  [15:0] in2,
  output z,
  output [15:0] result
);

  wire decoder_1_out1;
  wire [15:0] adder_sub_1_result, and_1_out, not_1_out, sll5bit_1_outdata, srl5bit_1_dataout;

  Decoder #(.select(3), .enable("false")) decoder_1 (
    .out1(decoder_1_out1), .sel(ALUop));  // open: out0, out2, out3, out4, out5, out6, out7
  assign not_1_out = ~in1;  // NOT_Gate not_1, 16 bits wide
  assign and_1_out = in1 & in2;  // AND_Gate and_1, 16 bits wide
  adder_sub adder_sub_1 (
    .A(in1), .B(in2), .sub(decoder_1_out1), .result(adder_sub_1_result), .z(z));  // open: unsigned_ovf, signed_ovf
  sll5bit sll5bit_1 (.data_In(in1), .sftmnt(in2), .outData(sll5bit_1_outdata));
  srl5bit srl5bit_1 (.dataIn(in1), .sftmnt(in2), .dataOut(srl5bit_1_dataout));
  Multiplexer #(.select(3), .width(16), .enable("false")) multiplexer_1 (
    .in0(adder_sub_1_result), .in1(adder_sub_1_result), .in2(sll5bit_1_outdata), .in3(srl5bit_1_dataout),
    .in4(and_1_out), .in5(not_1_out), .out(result), .sel(ALUop));  // open: in6, in7

  // Other names for the same wires on the sheet: op[2:0] = ALUop
endmodule

module adder_sub (
  input  [15:0] A,
  input  [15:0] B,
  input  sub,
  output unsigned_ovf,
  output signed_ovf,
  output [15:0] result,
  output z
);

  wire bit_adder_1_cout, bit_adder_2_cout, bit_adder_3_cout, bit_adder_4_cout, bit_adder_5_cout,
       bit_adder_6_cout, bit_adder_7_cout, bit_adder_8_cout, bit_adder_9_cout, bit_adder_10_cout,
       bit_adder_11_cout, bit_adder_12_cout, bit_adder_13_cout, bit_adder_14_cout, bit_adder_15_cout,
       or_1_out;

  bit_adder bit_adder_1 (.Cin(sub), .A(A[0]), .B(B[0]), .subi(sub), .sum(result[0]), .Cout(bit_adder_1_cout));
  bit_adder bit_adder_2 (
    .Cin(bit_adder_15_cout), .A(A[8]), .B(B[8]), .subi(sub), .sum(result[8]), .Cout(bit_adder_2_cout));
  bit_adder bit_adder_3 (
    .Cin(bit_adder_1_cout), .A(A[1]), .B(B[1]), .subi(sub), .sum(result[1]), .Cout(bit_adder_3_cout));
  bit_adder bit_adder_4 (
    .Cin(bit_adder_2_cout), .A(A[9]), .B(B[9]), .subi(sub), .sum(result[9]), .Cout(bit_adder_4_cout));
  bit_adder bit_adder_5 (
    .Cin(bit_adder_3_cout), .A(A[2]), .B(B[2]), .subi(sub), .sum(result[2]), .Cout(bit_adder_5_cout));
  bit_adder bit_adder_6 (
    .Cin(bit_adder_4_cout), .A(A[10]), .B(B[10]), .subi(sub), .sum(result[10]), .Cout(bit_adder_6_cout));
  bit_adder bit_adder_7 (
    .Cin(bit_adder_5_cout), .A(A[3]), .B(B[3]), .subi(sub), .sum(result[3]), .Cout(bit_adder_7_cout));
  bit_adder bit_adder_8 (
    .Cin(bit_adder_6_cout), .A(A[11]), .B(B[11]), .subi(sub), .sum(result[11]), .Cout(bit_adder_8_cout));
  bit_adder bit_adder_9 (
    .Cin(bit_adder_7_cout), .A(A[4]), .B(B[4]), .subi(sub), .sum(result[4]), .Cout(bit_adder_9_cout));
  bit_adder bit_adder_10 (
    .Cin(bit_adder_8_cout), .A(A[12]), .B(B[12]), .subi(sub), .sum(result[12]), .Cout(bit_adder_10_cout));
  bit_adder bit_adder_11 (
    .Cin(bit_adder_9_cout), .A(A[5]), .B(B[5]), .subi(sub), .sum(result[5]), .Cout(bit_adder_11_cout));
  bit_adder bit_adder_12 (
    .Cin(bit_adder_10_cout), .A(A[13]), .B(B[13]), .subi(sub), .sum(result[13]), .Cout(bit_adder_12_cout));
  or or_1 (or_1_out, result[0], result[1], result[2], result[3], result[4], result[5], result[6], result[7], result[8], result[9], result[10], result[11], result[12], result[13], result[14], result[15]);
  not not_1 (z, or_1_out);
  bit_adder bit_adder_13 (
    .Cin(bit_adder_11_cout), .A(A[6]), .B(B[6]), .subi(sub), .sum(result[6]), .Cout(bit_adder_13_cout));
  bit_adder bit_adder_14 (
    .Cin(bit_adder_12_cout), .A(A[14]), .B(B[14]), .subi(sub), .sum(result[14]), .Cout(bit_adder_14_cout));
  bit_adder bit_adder_15 (
    .Cin(bit_adder_13_cout), .A(A[7]), .B(B[7]), .subi(sub), .sum(result[7]), .Cout(bit_adder_15_cout));
  bit_adder bit_adder_16 (
    .Cin(bit_adder_14_cout), .A(A[15]), .B(B[15]), .subi(sub), .sum(result[15]), .Cout(unsigned_ovf));
  xor xor_1 (signed_ovf, bit_adder_14_cout, unsigned_ovf);

  // Other names for the same wires on the sheet: R0 = result[0]; R1 = result[1]; R2 = result[2]; R3 = result[3];
  //   R4 = result[4]; R5 = result[5]; R6 = result[6]; R7 = result[7]; R8 = result[8]; R9 = result[9];
  //   R10 = result[10]; R11 = result[11]; R12 = result[12]; R13 = result[13]; R14 = result[14]; R15 = result[15];
  //   subi = sub
endmodule

module bit_adder (
  input  Cin,
  input  A,
  input  B,
  input  subi,
  output sum,
  output Cout
);

  wire and_1_out, and_2_out, xor_1_out, xor_2_out;

  and and_1 (and_1_out, xor_1_out, A);
  xor xor_1 (xor_1_out, subi, B);
  or or_1 (Cout, and_1_out, and_2_out);
  xor xor_2 (xor_2_out, A, xor_1_out);
  and and_2 (and_2_out, xor_2_out, Cin);
  xor xor_3 (sum, Cin, xor_2_out);
endmodule

module sll5bit (
  input  [15:0] data_In,
  input  [15:0] sftmnt,
  output [15:0] outData
);

  wire multiplexer_1_out, multiplexer_2_out, multiplexer_3_out, multiplexer_4_out, multiplexer_5_out,
       multiplexer_6_out, multiplexer_7_out, multiplexer_8_out, multiplexer_9_out, multiplexer_10_out,
       multiplexer_11_out, multiplexer_12_out, multiplexer_13_out, multiplexer_14_out, multiplexer_15_out,
       multiplexer_16_out, multiplexer_17_out, multiplexer_18_out, multiplexer_19_out, multiplexer_20_out,
       multiplexer_21_out, multiplexer_22_out, multiplexer_23_out, multiplexer_24_out, multiplexer_25_out,
       multiplexer_26_out, multiplexer_27_out, multiplexer_28_out, multiplexer_29_out, multiplexer_30_out,
       multiplexer_31_out, multiplexer_32_out, multiplexer_33_out, multiplexer_34_out, multiplexer_35_out,
       multiplexer_36_out, multiplexer_37_out, multiplexer_38_out, multiplexer_39_out, multiplexer_40_out,
       multiplexer_41_out, multiplexer_42_out, multiplexer_43_out, multiplexer_44_out, multiplexer_45_out,
       multiplexer_46_out, multiplexer_47_out, multiplexer_48_out, multiplexer_49_out, multiplexer_50_out,
       multiplexer_51_out, multiplexer_52_out, multiplexer_53_out, multiplexer_54_out, multiplexer_55_out,
       multiplexer_56_out, multiplexer_57_out, multiplexer_58_out, multiplexer_59_out, multiplexer_60_out,
       multiplexer_61_out, multiplexer_62_out, multiplexer_63_out, multiplexer_64_out;

  Multiplexer #(.enable("false")) multiplexer_1 (
    .in0(data_In[15]), .in1(data_In[0]), .out(multiplexer_1_out), .sel(sftmnt[4]));
  Multiplexer #(.enable("false")) multiplexer_2 (
    .in0(data_In[14]), .in1(1'b0), .out(multiplexer_2_out), .sel(sftmnt[4]));
  Multiplexer #(.enable("false")) multiplexer_3 (
    .in0(data_In[13]), .in1(1'b0), .out(multiplexer_3_out), .sel(sftmnt[4]));
  Multiplexer #(.enable("false")) multiplexer_4 (
    .in0(data_In[12]), .in1(1'b0), .out(multiplexer_4_out), .sel(sftmnt[4]));
  Multiplexer #(.enable("false")) multiplexer_5 (
    .in0(data_In[11]), .in1(1'b0), .out(multiplexer_5_out), .sel(sftmnt[4]));
  Multiplexer #(.enable("false")) multiplexer_6 (
    .in0(data_In[10]), .in1(1'b0), .out(multiplexer_6_out), .sel(sftmnt[4]));
  Multiplexer #(.enable("false")) multiplexer_7 (
    .in0(data_In[9]), .in1(1'b0), .out(multiplexer_7_out), .sel(sftmnt[4]));
  Multiplexer #(.enable("false")) multiplexer_8 (
    .in0(data_In[8]), .in1(1'b0), .out(multiplexer_8_out), .sel(sftmnt[4]));
  Multiplexer #(.enable("false")) multiplexer_9 (
    .in0(data_In[7]), .in1(1'b0), .out(multiplexer_9_out), .sel(sftmnt[4]));
  Multiplexer #(.enable("false")) multiplexer_10 (
    .in0(data_In[6]), .in1(1'b0), .out(multiplexer_10_out), .sel(sftmnt[4]));
  Multiplexer #(.enable("false")) multiplexer_11 (
    .in0(data_In[5]), .in1(1'b0), .out(multiplexer_11_out), .sel(sftmnt[4]));
  Multiplexer #(.enable("false")) multiplexer_12 (
    .in0(data_In[4]), .in1(1'b0), .out(multiplexer_12_out), .sel(sftmnt[4]));
  Multiplexer #(.enable("false")) multiplexer_13 (
    .in0(data_In[3]), .in1(1'b0), .out(multiplexer_13_out), .sel(sftmnt[4]));
  Multiplexer #(.enable("false")) multiplexer_14 (
    .in0(data_In[2]), .in1(1'b0), .out(multiplexer_14_out), .sel(sftmnt[4]));
  Multiplexer #(.enable("false")) multiplexer_15 (
    .in0(data_In[1]), .in1(1'b0), .out(multiplexer_15_out), .sel(sftmnt[4]));
  Multiplexer #(.enable("false")) multiplexer_16 (
    .in0(data_In[0]), .in1(1'b0), .out(multiplexer_16_out), .sel(sftmnt[4]));
  Multiplexer #(.enable("false")) multiplexer_17 (
    .in0(multiplexer_1_out), .in1(multiplexer_9_out), .out(multiplexer_17_out), .sel(sftmnt[3]));
  Multiplexer #(.enable("false")) multiplexer_18 (
    .in0(multiplexer_2_out), .in1(multiplexer_10_out), .out(multiplexer_18_out), .sel(sftmnt[3]));
  Multiplexer #(.enable("false")) multiplexer_19 (
    .in0(multiplexer_3_out), .in1(multiplexer_11_out), .out(multiplexer_19_out), .sel(sftmnt[3]));
  Multiplexer #(.enable("false")) multiplexer_20 (
    .in0(multiplexer_4_out), .in1(multiplexer_12_out), .out(multiplexer_20_out), .sel(sftmnt[3]));
  Multiplexer #(.enable("false")) multiplexer_21 (
    .in0(multiplexer_5_out), .in1(multiplexer_13_out), .out(multiplexer_21_out), .sel(sftmnt[3]));
  Multiplexer #(.enable("false")) multiplexer_22 (
    .in0(multiplexer_6_out), .in1(multiplexer_14_out), .out(multiplexer_22_out), .sel(sftmnt[3]));
  Multiplexer #(.enable("false")) multiplexer_23 (
    .in0(multiplexer_7_out), .in1(multiplexer_15_out), .out(multiplexer_23_out), .sel(sftmnt[3]));
  Multiplexer #(.enable("false")) multiplexer_24 (
    .in0(multiplexer_8_out), .in1(multiplexer_16_out), .out(multiplexer_24_out), .sel(sftmnt[3]));
  Multiplexer #(.enable("false")) multiplexer_25 (
    .in0(multiplexer_9_out), .in1(1'b0), .out(multiplexer_25_out), .sel(sftmnt[3]));
  Multiplexer #(.enable("false")) multiplexer_26 (
    .in0(multiplexer_10_out), .in1(1'b0), .out(multiplexer_26_out), .sel(sftmnt[3]));
  Multiplexer #(.enable("false")) multiplexer_27 (
    .in0(multiplexer_11_out), .in1(1'b0), .out(multiplexer_27_out), .sel(sftmnt[3]));
  Multiplexer #(.enable("false")) multiplexer_28 (
    .in0(multiplexer_12_out), .in1(1'b0), .out(multiplexer_28_out), .sel(sftmnt[3]));
  Multiplexer #(.enable("false")) multiplexer_29 (
    .in0(multiplexer_13_out), .in1(1'b0), .out(multiplexer_29_out), .sel(sftmnt[3]));
  Multiplexer #(.enable("false")) multiplexer_30 (
    .in0(multiplexer_14_out), .in1(1'b0), .out(multiplexer_30_out), .sel(sftmnt[3]));
  Multiplexer #(.enable("false")) multiplexer_31 (
    .in0(multiplexer_15_out), .in1(1'b0), .out(multiplexer_31_out), .sel(sftmnt[3]));
  Multiplexer #(.enable("false")) multiplexer_32 (
    .in0(multiplexer_16_out), .in1(1'b0), .out(multiplexer_32_out), .sel(sftmnt[3]));
  Multiplexer #(.enable("false")) multiplexer_33 (
    .in0(multiplexer_17_out), .in1(multiplexer_21_out), .out(multiplexer_33_out), .sel(sftmnt[2]));
  Multiplexer #(.enable("false")) multiplexer_34 (
    .in0(multiplexer_18_out), .in1(multiplexer_22_out), .out(multiplexer_34_out), .sel(sftmnt[2]));
  Multiplexer #(.enable("false")) multiplexer_35 (
    .in0(multiplexer_19_out), .in1(multiplexer_23_out), .out(multiplexer_35_out), .sel(sftmnt[2]));
  Multiplexer #(.enable("false")) multiplexer_36 (
    .in0(multiplexer_20_out), .in1(multiplexer_24_out), .out(multiplexer_36_out), .sel(sftmnt[2]));
  Multiplexer #(.enable("false")) multiplexer_37 (
    .in0(multiplexer_21_out), .in1(multiplexer_25_out), .out(multiplexer_37_out), .sel(sftmnt[2]));
  Multiplexer #(.enable("false")) multiplexer_38 (
    .in0(multiplexer_22_out), .in1(multiplexer_26_out), .out(multiplexer_38_out), .sel(sftmnt[2]));
  Multiplexer #(.enable("false")) multiplexer_39 (
    .in0(multiplexer_23_out), .in1(multiplexer_27_out), .out(multiplexer_39_out), .sel(sftmnt[2]));
  Multiplexer #(.enable("false")) multiplexer_40 (
    .in0(multiplexer_24_out), .in1(multiplexer_28_out), .out(multiplexer_40_out), .sel(sftmnt[2]));
  Multiplexer #(.enable("false")) multiplexer_41 (
    .in0(multiplexer_25_out), .in1(multiplexer_29_out), .out(multiplexer_41_out), .sel(sftmnt[2]));
  Multiplexer #(.enable("false")) multiplexer_42 (
    .in0(multiplexer_26_out), .in1(multiplexer_30_out), .out(multiplexer_42_out), .sel(sftmnt[2]));
  Multiplexer #(.enable("false")) multiplexer_43 (
    .in0(multiplexer_27_out), .in1(multiplexer_31_out), .out(multiplexer_43_out), .sel(sftmnt[2]));
  Multiplexer #(.enable("false")) multiplexer_44 (
    .in0(multiplexer_28_out), .in1(multiplexer_32_out), .out(multiplexer_44_out), .sel(sftmnt[2]));
  Multiplexer #(.enable("false")) multiplexer_45 (
    .in0(multiplexer_29_out), .in1(1'b0), .out(multiplexer_45_out), .sel(sftmnt[2]));
  Multiplexer #(.enable("false")) multiplexer_46 (
    .in0(multiplexer_30_out), .in1(1'b0), .out(multiplexer_46_out), .sel(sftmnt[2]));
  Multiplexer #(.enable("false")) multiplexer_47 (
    .in0(multiplexer_31_out), .in1(1'b0), .out(multiplexer_47_out), .sel(sftmnt[2]));
  Multiplexer #(.enable("false")) multiplexer_48 (
    .in0(multiplexer_32_out), .in1(1'b0), .out(multiplexer_48_out), .sel(sftmnt[2]));
  Multiplexer #(.enable("false")) multiplexer_49 (
    .in0(multiplexer_33_out), .in1(multiplexer_35_out), .out(multiplexer_49_out), .sel(sftmnt[1]));
  Multiplexer #(.enable("false")) multiplexer_50 (
    .in0(multiplexer_34_out), .in1(multiplexer_36_out), .out(multiplexer_50_out), .sel(sftmnt[1]));
  Multiplexer #(.enable("false")) multiplexer_51 (
    .in0(multiplexer_35_out), .in1(multiplexer_37_out), .out(multiplexer_51_out), .sel(sftmnt[1]));
  Multiplexer #(.enable("false")) multiplexer_52 (
    .in0(multiplexer_36_out), .in1(multiplexer_38_out), .out(multiplexer_52_out), .sel(sftmnt[1]));
  Multiplexer #(.enable("false")) multiplexer_53 (
    .in0(multiplexer_37_out), .in1(multiplexer_39_out), .out(multiplexer_53_out), .sel(sftmnt[1]));
  Multiplexer #(.enable("false")) multiplexer_54 (
    .in0(multiplexer_38_out), .in1(multiplexer_40_out), .out(multiplexer_54_out), .sel(sftmnt[1]));
  Multiplexer #(.enable("false")) multiplexer_55 (
    .in0(multiplexer_39_out), .in1(multiplexer_41_out), .out(multiplexer_55_out), .sel(sftmnt[1]));
  Multiplexer #(.enable("false")) multiplexer_56 (
    .in0(multiplexer_40_out), .in1(multiplexer_42_out), .out(multiplexer_56_out), .sel(sftmnt[1]));
  Multiplexer #(.enable("false")) multiplexer_57 (
    .in0(multiplexer_41_out), .in1(multiplexer_43_out), .out(multiplexer_57_out), .sel(sftmnt[1]));
  Multiplexer #(.enable("false")) multiplexer_58 (
    .in0(multiplexer_42_out), .in1(multiplexer_44_out), .out(multiplexer_58_out), .sel(sftmnt[1]));
  Multiplexer #(.enable("false")) multiplexer_59 (
    .in0(multiplexer_43_out), .in1(multiplexer_45_out), .out(multiplexer_59_out), .sel(sftmnt[1]));
  Multiplexer #(.enable("false")) multiplexer_60 (
    .in0(multiplexer_44_out), .in1(multiplexer_46_out), .out(multiplexer_60_out), .sel(sftmnt[1]));
  Multiplexer #(.enable("false")) multiplexer_61 (
    .in0(multiplexer_45_out), .in1(multiplexer_47_out), .out(multiplexer_61_out), .sel(sftmnt[1]));
  Multiplexer #(.enable("false")) multiplexer_62 (
    .in0(multiplexer_46_out), .in1(multiplexer_48_out), .out(multiplexer_62_out), .sel(sftmnt[1]));
  Multiplexer #(.enable("false")) multiplexer_63 (
    .in0(multiplexer_47_out), .in1(1'b0), .out(multiplexer_63_out), .sel(sftmnt[1]));
  Multiplexer #(.enable("false")) multiplexer_64 (
    .in0(multiplexer_48_out), .in1(1'b0), .out(multiplexer_64_out), .sel(sftmnt[1]));
  Multiplexer #(.enable("false")) multiplexer_65 (
    .in0(multiplexer_49_out), .in1(multiplexer_50_out), .out(outData[15]), .sel(sftmnt[0]));
  Multiplexer #(.enable("false")) multiplexer_66 (
    .in0(multiplexer_50_out), .in1(multiplexer_51_out), .out(outData[14]), .sel(sftmnt[0]));
  Multiplexer #(.enable("false")) multiplexer_67 (
    .in0(multiplexer_51_out), .in1(multiplexer_52_out), .out(outData[13]), .sel(sftmnt[0]));
  Multiplexer #(.enable("false")) multiplexer_68 (
    .in0(multiplexer_52_out), .in1(multiplexer_53_out), .out(outData[12]), .sel(sftmnt[0]));
  Multiplexer #(.enable("false")) multiplexer_69 (
    .in0(multiplexer_53_out), .in1(multiplexer_54_out), .out(outData[11]), .sel(sftmnt[0]));
  Multiplexer #(.enable("false")) multiplexer_70 (
    .in0(multiplexer_54_out), .in1(multiplexer_55_out), .out(outData[10]), .sel(sftmnt[0]));
  Multiplexer #(.enable("false")) multiplexer_71 (
    .in0(multiplexer_55_out), .in1(multiplexer_56_out), .out(outData[9]), .sel(sftmnt[0]));
  Multiplexer #(.enable("false")) multiplexer_72 (
    .in0(multiplexer_56_out), .in1(multiplexer_57_out), .out(outData[8]), .sel(sftmnt[0]));
  Multiplexer #(.enable("false")) multiplexer_73 (
    .in0(multiplexer_57_out), .in1(multiplexer_58_out), .out(outData[7]), .sel(sftmnt[0]));
  Multiplexer #(.enable("false")) multiplexer_74 (
    .in0(multiplexer_58_out), .in1(multiplexer_59_out), .out(outData[6]), .sel(sftmnt[0]));
  Multiplexer #(.enable("false")) multiplexer_75 (
    .in0(multiplexer_59_out), .in1(multiplexer_60_out), .out(outData[5]), .sel(sftmnt[0]));
  Multiplexer #(.enable("false")) multiplexer_76 (
    .in0(multiplexer_60_out), .in1(multiplexer_61_out), .out(outData[4]), .sel(sftmnt[0]));
  Multiplexer #(.enable("false")) multiplexer_77 (
    .in0(multiplexer_61_out), .in1(multiplexer_62_out), .out(outData[3]), .sel(sftmnt[0]));
  Multiplexer #(.enable("false")) multiplexer_78 (
    .in0(multiplexer_62_out), .in1(multiplexer_63_out), .out(outData[2]), .sel(sftmnt[0]));
  Multiplexer #(.enable("false")) multiplexer_79 (
    .in0(multiplexer_63_out), .in1(multiplexer_64_out), .out(outData[1]), .sel(sftmnt[0]));
  Multiplexer #(.enable("false")) multiplexer_80 (
    .in0(multiplexer_64_out), .in1(1'b0), .out(outData[0]), .sel(sftmnt[0]));

  // Other names for the same wires on the sheet: d0 = data_In[0]; d1 = data_In[1]; d2 = data_In[2]; d3 = data_In[3];
  //   d4 = data_In[4]; d5 = data_In[5]; d6 = data_In[6]; d7 = data_In[7]; d8 = data_In[8]; d9 = data_In[9];
  //   d10 = data_In[10]; d11 = data_In[11]; d12 = data_In[12]; d13 = data_In[13]; d14 = data_In[14];
  //   d15 = data_In[15]
endmodule

module srl5bit (
  input  [15:0] dataIn,
  input  [15:0] sftmnt,
  output [15:0] dataOut
);

  wire multiplexer_1_out, multiplexer_2_out, multiplexer_3_out, multiplexer_4_out, multiplexer_5_out,
       multiplexer_6_out, multiplexer_7_out, multiplexer_8_out, multiplexer_9_out, multiplexer_10_out,
       multiplexer_11_out, multiplexer_12_out, multiplexer_13_out, multiplexer_14_out, multiplexer_15_out,
       multiplexer_16_out, multiplexer_17_out, multiplexer_18_out, multiplexer_19_out, multiplexer_20_out,
       multiplexer_21_out, multiplexer_22_out, multiplexer_23_out, multiplexer_24_out, multiplexer_25_out,
       multiplexer_26_out, multiplexer_27_out, multiplexer_28_out, multiplexer_29_out, multiplexer_30_out,
       multiplexer_31_out, multiplexer_32_out, multiplexer_33_out, multiplexer_34_out, multiplexer_35_out,
       multiplexer_36_out, multiplexer_37_out, multiplexer_38_out, multiplexer_39_out, multiplexer_40_out,
       multiplexer_41_out, multiplexer_42_out, multiplexer_43_out, multiplexer_44_out, multiplexer_45_out,
       multiplexer_46_out, multiplexer_47_out, multiplexer_48_out, multiplexer_49_out, multiplexer_50_out,
       multiplexer_51_out, multiplexer_52_out, multiplexer_53_out, multiplexer_54_out, multiplexer_55_out,
       multiplexer_56_out, multiplexer_57_out, multiplexer_58_out, multiplexer_59_out, multiplexer_60_out,
       multiplexer_61_out, multiplexer_62_out, multiplexer_63_out, multiplexer_64_out;

  Multiplexer #(.enable("false")) multiplexer_1 (
    .in0(dataIn[15]), .in1(1'b0), .out(multiplexer_1_out), .sel(sftmnt[4]));
  Multiplexer #(.enable("false")) multiplexer_2 (
    .in0(dataIn[14]), .in1(1'b0), .out(multiplexer_2_out), .sel(sftmnt[4]));
  Multiplexer #(.enable("false")) multiplexer_3 (
    .in0(dataIn[13]), .in1(1'b0), .out(multiplexer_3_out), .sel(sftmnt[4]));
  Multiplexer #(.enable("false")) multiplexer_4 (
    .in0(dataIn[12]), .in1(1'b0), .out(multiplexer_4_out), .sel(sftmnt[4]));
  Multiplexer #(.enable("false")) multiplexer_5 (
    .in0(dataIn[11]), .in1(1'b0), .out(multiplexer_5_out), .sel(sftmnt[4]));
  Multiplexer #(.enable("false")) multiplexer_6 (
    .in0(dataIn[10]), .in1(1'b0), .out(multiplexer_6_out), .sel(sftmnt[4]));
  Multiplexer #(.enable("false")) multiplexer_7 (.in0(dataIn[9]), .in1(1'b0), .out(multiplexer_7_out), .sel(sftmnt[4]));
  Multiplexer #(.enable("false")) multiplexer_8 (.in0(dataIn[8]), .in1(1'b0), .out(multiplexer_8_out), .sel(sftmnt[4]));
  Multiplexer #(.enable("false")) multiplexer_9 (.in0(dataIn[7]), .in1(1'b0), .out(multiplexer_9_out), .sel(sftmnt[4]));
  Multiplexer #(.enable("false")) multiplexer_10 (
    .in0(dataIn[6]), .in1(1'b0), .out(multiplexer_10_out), .sel(sftmnt[4]));
  Multiplexer #(.enable("false")) multiplexer_11 (
    .in0(dataIn[5]), .in1(1'b0), .out(multiplexer_11_out), .sel(sftmnt[4]));
  Multiplexer #(.enable("false")) multiplexer_12 (
    .in0(dataIn[4]), .in1(1'b0), .out(multiplexer_12_out), .sel(sftmnt[4]));
  Multiplexer #(.enable("false")) multiplexer_13 (
    .in0(dataIn[3]), .in1(1'b0), .out(multiplexer_13_out), .sel(sftmnt[4]));
  Multiplexer #(.enable("false")) multiplexer_14 (
    .in0(dataIn[2]), .in1(1'b0), .out(multiplexer_14_out), .sel(sftmnt[4]));
  Multiplexer #(.enable("false")) multiplexer_15 (
    .in0(dataIn[1]), .in1(1'b0), .out(multiplexer_15_out), .sel(sftmnt[4]));
  Multiplexer #(.enable("false")) multiplexer_16 (
    .in0(dataIn[0]), .in1(dataIn[15]), .out(multiplexer_16_out), .sel(sftmnt[4]));
  Multiplexer #(.enable("false")) multiplexer_17 (
    .in0(multiplexer_1_out), .in1(1'b0), .out(multiplexer_17_out), .sel(sftmnt[3]));
  Multiplexer #(.enable("false")) multiplexer_18 (
    .in0(multiplexer_2_out), .in1(1'b0), .out(multiplexer_18_out), .sel(sftmnt[3]));
  Multiplexer #(.enable("false")) multiplexer_19 (
    .in0(multiplexer_3_out), .in1(1'b0), .out(multiplexer_19_out), .sel(sftmnt[3]));
  Multiplexer #(.enable("false")) multiplexer_20 (
    .in0(multiplexer_4_out), .in1(1'b0), .out(multiplexer_20_out), .sel(sftmnt[3]));
  Multiplexer #(.enable("false")) multiplexer_21 (
    .in0(multiplexer_5_out), .in1(1'b0), .out(multiplexer_21_out), .sel(sftmnt[3]));
  Multiplexer #(.enable("false")) multiplexer_22 (
    .in0(multiplexer_6_out), .in1(1'b0), .out(multiplexer_22_out), .sel(sftmnt[3]));
  Multiplexer #(.enable("false")) multiplexer_23 (
    .in0(multiplexer_7_out), .in1(1'b0), .out(multiplexer_23_out), .sel(sftmnt[3]));
  Multiplexer #(.enable("false")) multiplexer_24 (
    .in0(multiplexer_8_out), .in1(1'b0), .out(multiplexer_24_out), .sel(sftmnt[3]));
  Multiplexer #(.enable("false")) multiplexer_25 (
    .in0(multiplexer_9_out), .in1(multiplexer_1_out), .out(multiplexer_25_out), .sel(sftmnt[3]));
  Multiplexer #(.enable("false")) multiplexer_26 (
    .in0(multiplexer_10_out), .in1(multiplexer_2_out), .out(multiplexer_26_out), .sel(sftmnt[3]));
  Multiplexer #(.enable("false")) multiplexer_27 (
    .in0(multiplexer_11_out), .in1(multiplexer_3_out), .out(multiplexer_27_out), .sel(sftmnt[3]));
  Multiplexer #(.enable("false")) multiplexer_28 (
    .in0(multiplexer_12_out), .in1(multiplexer_4_out), .out(multiplexer_28_out), .sel(sftmnt[3]));
  Multiplexer #(.enable("false")) multiplexer_29 (
    .in0(multiplexer_13_out), .in1(multiplexer_5_out), .out(multiplexer_29_out), .sel(sftmnt[3]));
  Multiplexer #(.enable("false")) multiplexer_30 (
    .in0(multiplexer_14_out), .in1(multiplexer_6_out), .out(multiplexer_30_out), .sel(sftmnt[3]));
  Multiplexer #(.enable("false")) multiplexer_31 (
    .in0(multiplexer_15_out), .in1(multiplexer_7_out), .out(multiplexer_31_out), .sel(sftmnt[3]));
  Multiplexer #(.enable("false")) multiplexer_32 (
    .in0(multiplexer_16_out), .in1(multiplexer_8_out), .out(multiplexer_32_out), .sel(sftmnt[3]));
  Multiplexer #(.enable("false")) multiplexer_33 (
    .in0(multiplexer_17_out), .in1(1'b0), .out(multiplexer_33_out), .sel(sftmnt[2]));
  Multiplexer #(.enable("false")) multiplexer_34 (
    .in0(multiplexer_18_out), .in1(1'b0), .out(multiplexer_34_out), .sel(sftmnt[2]));
  Multiplexer #(.enable("false")) multiplexer_35 (
    .in0(multiplexer_19_out), .in1(1'b0), .out(multiplexer_35_out), .sel(sftmnt[2]));
  Multiplexer #(.enable("false")) multiplexer_36 (
    .in0(multiplexer_20_out), .in1(1'b0), .out(multiplexer_36_out), .sel(sftmnt[2]));
  Multiplexer #(.enable("false")) multiplexer_37 (
    .in0(multiplexer_21_out), .in1(multiplexer_17_out), .out(multiplexer_37_out), .sel(sftmnt[2]));
  Multiplexer #(.enable("false")) multiplexer_38 (
    .in0(multiplexer_22_out), .in1(multiplexer_18_out), .out(multiplexer_38_out), .sel(sftmnt[2]));
  Multiplexer #(.enable("false")) multiplexer_39 (
    .in0(multiplexer_23_out), .in1(multiplexer_19_out), .out(multiplexer_39_out), .sel(sftmnt[2]));
  Multiplexer #(.enable("false")) multiplexer_40 (
    .in0(multiplexer_24_out), .in1(multiplexer_20_out), .out(multiplexer_40_out), .sel(sftmnt[2]));
  Multiplexer #(.enable("false")) multiplexer_41 (
    .in0(multiplexer_25_out), .in1(multiplexer_21_out), .out(multiplexer_41_out), .sel(sftmnt[2]));
  Multiplexer #(.enable("false")) multiplexer_42 (
    .in0(multiplexer_26_out), .in1(multiplexer_22_out), .out(multiplexer_42_out), .sel(sftmnt[2]));
  Multiplexer #(.enable("false")) multiplexer_43 (
    .in0(multiplexer_27_out), .in1(multiplexer_23_out), .out(multiplexer_43_out), .sel(sftmnt[2]));
  Multiplexer #(.enable("false")) multiplexer_44 (
    .in0(multiplexer_28_out), .in1(multiplexer_24_out), .out(multiplexer_44_out), .sel(sftmnt[2]));
  Multiplexer #(.enable("false")) multiplexer_45 (
    .in0(multiplexer_29_out), .in1(multiplexer_25_out), .out(multiplexer_45_out), .sel(sftmnt[2]));
  Multiplexer #(.enable("false")) multiplexer_46 (
    .in0(multiplexer_30_out), .in1(multiplexer_26_out), .out(multiplexer_46_out), .sel(sftmnt[2]));
  Multiplexer #(.enable("false")) multiplexer_47 (
    .in0(multiplexer_31_out), .in1(multiplexer_27_out), .out(multiplexer_47_out), .sel(sftmnt[2]));
  Multiplexer #(.enable("false")) multiplexer_48 (
    .in0(multiplexer_32_out), .in1(multiplexer_28_out), .out(multiplexer_48_out), .sel(sftmnt[2]));
  Multiplexer #(.enable("false")) multiplexer_49 (
    .in0(multiplexer_33_out), .in1(1'b0), .out(multiplexer_49_out), .sel(sftmnt[1]));
  Multiplexer #(.enable("false")) multiplexer_50 (
    .in0(multiplexer_34_out), .in1(1'b0), .out(multiplexer_50_out), .sel(sftmnt[1]));
  Multiplexer #(.enable("false")) multiplexer_51 (
    .in0(multiplexer_35_out), .in1(multiplexer_33_out), .out(multiplexer_51_out), .sel(sftmnt[1]));
  Multiplexer #(.enable("false")) multiplexer_52 (
    .in0(multiplexer_36_out), .in1(multiplexer_34_out), .out(multiplexer_52_out), .sel(sftmnt[1]));
  Multiplexer #(.enable("false")) multiplexer_53 (
    .in0(multiplexer_37_out), .in1(multiplexer_35_out), .out(multiplexer_53_out), .sel(sftmnt[1]));
  Multiplexer #(.enable("false")) multiplexer_54 (
    .in0(multiplexer_38_out), .in1(multiplexer_36_out), .out(multiplexer_54_out), .sel(sftmnt[1]));
  Multiplexer #(.enable("false")) multiplexer_55 (
    .in0(multiplexer_39_out), .in1(multiplexer_37_out), .out(multiplexer_55_out), .sel(sftmnt[1]));
  Multiplexer #(.enable("false")) multiplexer_56 (
    .in0(multiplexer_40_out), .in1(multiplexer_38_out), .out(multiplexer_56_out), .sel(sftmnt[1]));
  Multiplexer #(.enable("false")) multiplexer_57 (
    .in0(multiplexer_41_out), .in1(multiplexer_39_out), .out(multiplexer_57_out), .sel(sftmnt[1]));
  Multiplexer #(.enable("false")) multiplexer_58 (
    .in0(multiplexer_42_out), .in1(multiplexer_40_out), .out(multiplexer_58_out), .sel(sftmnt[1]));
  Multiplexer #(.enable("false")) multiplexer_59 (
    .in0(multiplexer_43_out), .in1(multiplexer_41_out), .out(multiplexer_59_out), .sel(sftmnt[1]));
  Multiplexer #(.enable("false")) multiplexer_60 (
    .in0(multiplexer_44_out), .in1(multiplexer_42_out), .out(multiplexer_60_out), .sel(sftmnt[1]));
  Multiplexer #(.enable("false")) multiplexer_61 (
    .in0(multiplexer_45_out), .in1(multiplexer_43_out), .out(multiplexer_61_out), .sel(sftmnt[1]));
  Multiplexer #(.enable("false")) multiplexer_62 (
    .in0(multiplexer_46_out), .in1(multiplexer_44_out), .out(multiplexer_62_out), .sel(sftmnt[1]));
  Multiplexer #(.enable("false")) multiplexer_63 (
    .in0(multiplexer_47_out), .in1(multiplexer_45_out), .out(multiplexer_63_out), .sel(sftmnt[1]));
  Multiplexer #(.enable("false")) multiplexer_64 (
    .in0(multiplexer_48_out), .in1(multiplexer_46_out), .out(multiplexer_64_out), .sel(sftmnt[1]));
  Multiplexer #(.enable("false")) multiplexer_65 (
    .in0(multiplexer_49_out), .in1(1'b0), .out(dataOut[15]), .sel(sftmnt[0]));
  Multiplexer #(.enable("false")) multiplexer_66 (
    .in0(multiplexer_50_out), .in1(multiplexer_49_out), .out(dataOut[14]), .sel(sftmnt[0]));
  Multiplexer #(.enable("false")) multiplexer_67 (
    .in0(multiplexer_51_out), .in1(multiplexer_50_out), .out(dataOut[13]), .sel(sftmnt[0]));
  Multiplexer #(.enable("false")) multiplexer_68 (
    .in0(multiplexer_52_out), .in1(multiplexer_51_out), .out(dataOut[12]), .sel(sftmnt[0]));
  Multiplexer #(.enable("false")) multiplexer_69 (
    .in0(multiplexer_53_out), .in1(multiplexer_52_out), .out(dataOut[11]), .sel(sftmnt[0]));
  Multiplexer #(.enable("false")) multiplexer_70 (
    .in0(multiplexer_54_out), .in1(multiplexer_53_out), .out(dataOut[10]), .sel(sftmnt[0]));
  Multiplexer #(.enable("false")) multiplexer_71 (
    .in0(multiplexer_55_out), .in1(multiplexer_54_out), .out(dataOut[9]), .sel(sftmnt[0]));
  Multiplexer #(.enable("false")) multiplexer_72 (
    .in0(multiplexer_56_out), .in1(multiplexer_55_out), .out(dataOut[8]), .sel(sftmnt[0]));
  Multiplexer #(.enable("false")) multiplexer_73 (
    .in0(multiplexer_57_out), .in1(multiplexer_56_out), .out(dataOut[7]), .sel(sftmnt[0]));
  Multiplexer #(.enable("false")) multiplexer_74 (
    .in0(multiplexer_58_out), .in1(multiplexer_57_out), .out(dataOut[6]), .sel(sftmnt[0]));
  Multiplexer #(.enable("false")) multiplexer_75 (
    .in0(multiplexer_59_out), .in1(multiplexer_58_out), .out(dataOut[5]), .sel(sftmnt[0]));
  Multiplexer #(.enable("false")) multiplexer_76 (
    .in0(multiplexer_60_out), .in1(multiplexer_59_out), .out(dataOut[4]), .sel(sftmnt[0]));
  Multiplexer #(.enable("false")) multiplexer_77 (
    .in0(multiplexer_61_out), .in1(multiplexer_60_out), .out(dataOut[3]), .sel(sftmnt[0]));
  Multiplexer #(.enable("false")) multiplexer_78 (
    .in0(multiplexer_62_out), .in1(multiplexer_61_out), .out(dataOut[2]), .sel(sftmnt[0]));
  Multiplexer #(.enable("false")) multiplexer_79 (
    .in0(multiplexer_63_out), .in1(multiplexer_62_out), .out(dataOut[1]), .sel(sftmnt[0]));
  Multiplexer #(.enable("false")) multiplexer_80 (
    .in0(multiplexer_64_out), .in1(multiplexer_63_out), .out(dataOut[0]), .sel(sftmnt[0]));

  // Other names for the same wires on the sheet: d0 = dataIn[0]; d1 = dataIn[1]; d2 = dataIn[2]; d3 = dataIn[3];
  //   d4 = dataIn[4]; d5 = dataIn[5]; d6 = dataIn[6]; d7 = dataIn[7]; d8 = dataIn[8]; d9 = dataIn[9];
  //   d10 = dataIn[10]; d11 = dataIn[11]; d12 = dataIn[12]; d13 = dataIn[13]; d14 = dataIn[14]; d15 = dataIn[15]
endmodule

module DRAM (
  input  [15:0] addrIn,
  input  DMwe,
  input  clk,
  input  [15:0] dataIn,
  output [15:0] dataOut
);

  wire memory_latch_1_oe_latched, memory_latch_1_we_latched, not_1_out;
  wire [15:0] memory_latch_1_address_latched, memory_latch_1_data_in_latched;

  not not_1 (not_1_out, clk);
  memory_latch memory_latch_1 (
    .address(addrIn), .WE(DMwe), .clk(not_1_out), .data_in(dataIn),
    .address_latched(memory_latch_1_address_latched), .WE_latched(memory_latch_1_we_latched),
    .OE_latched(memory_latch_1_oe_latched), .data_in_latched(memory_latch_1_data_in_latched));
  RAM #(.addrWidth(16), .dataWidth(16), .trigger("high"), .databus("bibus")) ram_1 (
    .addr(memory_latch_1_address_latched), .we(memory_latch_1_we_latched), .oe(memory_latch_1_oe_latched),
    .din(memory_latch_1_data_in_latched), .dout(dataOut));
endmodule

module memory_latch (
  input  [15:0] address,
  input  WE,
  input  clk,
  input  [15:0] data_in,
  output [15:0] address_latched,
  output WE_latched,
  output OE_latched,
  output [15:0] data_in_latched
);

  wire DMwe_latch_q;
  wire [15:0] addr_latch_q;

  Register #(.width(16), .trigger("falling")) addr_latch (
    .D(address), .en(WE), .clk(clk), .Q(addr_latch_q));  // open: clr
  D_Flip_Flop #(.trigger("falling")) DMwe_latch (.D(WE), .clk(clk), .Q(DMwe_latch_q));  // open: Qn, preset, reset
  Register #(.width(16), .trigger("falling")) data_to_be_written (
    .D(data_in), .en(WE), .clk(clk), .Q(data_in_latched));  // open: clr
  Multiplexer #(.width(16), .enable("false")) multiplexer_1 (
    .in0(address), .in1(addr_latch_q), .out(address_latched), .sel(DMwe_latch_q));
  and and_1 (WE_latched, clk, DMwe_latch_q);
  not not_1 (OE_latched, WE_latched);
endmodule

module adder_pc (
  input  [15:0] pc_val,
  output [15:0] out_2
);

  adder_sub adder_sub_1 (.A(pc_val), .B(16'h1), .result(out_2));  // open: sub, unsigned_ovf, signed_ovf, z
endmodule

module sign_extender (
  input  [5:0] in_ext,
  output [15:0] out_ext
);

  and and_1 (out_ext[15], in_ext[5], 1'b1);

  assign out_ext[14:0] = {{9{out_ext[15]}}, in_ext};
endmodule

module zero_extender (
  input  [11:0] in_1,
  output [15:0] out_2
);


  assign out_2 = {4'b0000, in_1};
endmodule
